# Fritzing sketch build-example (saved by Fritzing 0.9.4)
breadboards: 1

parts:
  Part1 = Arduino Nano (Rev3.0)
  S1 = Pushbutton [package="[THT]"]
  S2 = Pushbutton [package="[THT]"]
  S3 = Pushbutton [package="[THT]"]
  R1 = Resistor [tolerance=±5% resistance=220 package=THT]
  R2 = Resistor [tolerance=±5% resistance=220 package=THT]
  R3 = Resistor [tolerance=±5% resistance=220 package=THT]

nets:
  N1: Part1.GND, R1.Pin_0, R2.Pin_0, R3.Pin_0
  N2: Part1.D2, S1.Pin_3, S1.Pin_4, R3.Pin_1
  N3: Part1.D3, S2.Pin_3, S2.Pin_4, R2.Pin_1
  N4: Part1.D4, S3.Pin_3, S3.Pin_4, R1.Pin_1
  N5: Part1.5V, S1.Pin_1, S1.Pin_2, S2.Pin_1, S2.Pin_2, S3.Pin_1, S3.Pin_2
